# Fritzing sketch connections (saved by Fritzing 0.9.4)

parts:
  XIAO_ESP32S1 = XIAO ESP32S3 [package="DIP (Dual Inline) [THT]"]
  S1 = Pushbutton [package="[THT]"]
  A1 = lcd color display 1.3in 240x240 7pin interface [package=THT]
  RE1 = Rotary Encoder [package=THT]
  LED1 = smd LED [color="White (4500K)" package="0805 [SMD]"]
  LED2 = smd LED [color="White (4500K)" package="0805 [SMD]"]
  R1 = Resistor [tolerance=±5% resistance=100 package=THT]
  R2 = Resistor [tolerance=±5% resistance=100 package=THT]

nets:
  N1: XIAO_ESP32S1.D0, A1.BLK
  N2: XIAO_ESP32S1.D1, A1.DC
  N3: XIAO_ESP32S1.D2, A1.RES
  N4: XIAO_ESP32S1.D3, R1.Pin_1, R2.Pin_1
  N5: XIAO_ESP32S1.D4, S1.Pin_3, S1.Pin_4
  N6: XIAO_ESP32S1.D5, RE1.EncoderPinA
  N7: XIAO_ESP32S1.D6, RE1.EncoderPinB
  N8: XIAO_ESP32S1.D7, RE1.SwitchPinE
  N9: XIAO_ESP32S1.D8, A1.SCL
  N10: XIAO_ESP32S1.D10, A1.SDA
  3V3: XIAO_ESP32S1.3V3, A1.VCC
  N11: XIAO_ESP32S1.GND, RE1.SwitchrPinD
  N12: A1.GND, LED2.cathode
  N13: RE1.EncoderPinC, LED1.cathode

notes:
  GND
  VCC
  SCL
  SDA
  RST
  DC
  CS
  2.0" TFT LCD (ST7789VW)

custom parts:
  XIAO ESP32S3: Seeed Studio XIAO ESP32S3 leverages 240MHz Xtensa 32-bit LX7 dual-core processor, supporting both WiFi and BLE 5.0 wireless connectivities, a 2.4GHz Rod antenna, allows for deep sleep mode with power consumption as low as 14μA while supporting lithium battery charging management. Ideal for the Internet of Things, Smart Homes, Wireless wearable devices, Robotics, etc.
  lcd color display 1.3in 240x240 7pin interface: 1.3 Inch Color 240 x 240 IPS TFT LCD Display Screen Module Board 7 Pin 4 Wire ST7789VW Drive IC SPI interface.
  Rotary Encoder: Rotary Encoder from ALPSec11e with switch.
